// Logisim project Boolean Logic - APP Virtual Test.circ as structural Verilog: 1 circuit, main circuit main
module main (
  input  A,
  input  B,
  input  C
);

  wire and_1_out, and_2_out, and_3_out, or_1_out, or_2_out, or_3_out;

  or or_1 (or_1_out, B, C);
  or or_2 (or_2_out, A, C);
  and and_1 (and_1_out, A, B);
  and and_2 (and_2_out, A, C);
  and and_3 (and_3_out, B, C);
  or or_3 (or_3_out, and_1_out, and_2_out, and_3_out);
  LED Alarm_1 (.in(or_1_out));
  LED Alarm_2 (.in(or_2_out));
  LED Alarm_3 (.in(or_3_out));
endmodule
