// Logisim project Exercise 6 - 2 4 Binary Decoder.circ as structural Verilog: 1 circuit, main circuit main
module main (
  input  A,
  input  B
);

  wire and_1_out, and_2_out, and_3_out, and_4_out, not_1_out, not_2_out;

  not not_1 (not_1_out, A);
  not not_2 (not_2_out, B);
  and and_1 (and_1_out, not_2_out, not_2_out, not_1_out);
  and and_2 (and_2_out, A, not_2_out);
  and and_3 (and_3_out, B, not_1_out);
  and and_4 (and_4_out, A, B);
  LED D0 (.in(and_1_out));
  LED D1 (.in(and_2_out));
  LED D2 (.in(and_3_out));
  LED D3 (.in(and_4_out));
endmodule
