// Logisim project Summative - Decoder Project Logism.circ as structural Verilog: 1 circuit, main circuit main
module main (
  input  A,
  input  B,
  input  B_2,
  input  C,
  input  D
);

  wire and_1_out, and_2_out, and_3_out, and_4_out, and_5_out, and_6_out, and_7_out, and_8_out, and_9_out,
       and_10_out, and_11_out, and_12_out, and_13_out, and_14_out, and_15_out, and_16_out, and_17_out,
       and_18_out, and_19_out, and_20_out, nand_1_out, not_1_out, not_2_out, not_3_out, not_4_out, or_1_out,
       or_2_out, or_3_out, or_4_out, or_5_out, or_6_out, or_7_out, or_8_out;

  not not_1 (not_1_out, A);
  not not_2 (not_2_out, B_2);
  not not_3 (not_3_out, C);
  not not_4 (not_4_out, D);
  and and_1 (and_1_out, A, B_2);
  and and_2 (and_2_out, not_1_out, not_2_out, not_3_out);
  or or_1 (or_1_out, A, B_2, C);
  nand nand_1 (nand_1_out, A, B_2);
  and and_3 (and_3_out, not_1_out, not_2_out, C, D);
  and and_4 (and_4_out, A, B_2, not_3_out, D);
  and and_5 (and_5_out, not_1_out, B_2, C, not_4_out);
  and and_6 (and_6_out, not_1_out, B_2, C, D);
  and and_7 (and_7_out, A, not_2_out, not_3_out, not_4_out);
  and and_8 (and_8_out, not_1_out, B_2, not_3_out, not_4_out);
  and and_9 (and_9_out, A, B_2, C, not_4_out);
  and and_10 (and_10_out, A, not_3_out, D);
  and and_11 (and_11_out, not_1_out, not_2_out, C, D);
  and and_12 (and_12_out, not_1_out, B_2, C, not_4_out);
  and and_13 (and_13_out, not_1_out, B_2, C);
  and and_14 (and_14_out, not_1_out, B_2, not_3_out);
  and and_15 (and_15_out, A, not_3_out, D);
  and and_16 (and_16_out, not_1_out, not_2_out, C, D);
  and and_17 (and_17_out, A, B_2, C);
  and and_18 (and_18_out, not_1_out, not_2_out, C);
  and and_19 (and_19_out, A, B_2, not_3_out);
  and and_20 (and_20_out, A, not_3_out, D);
  or or_2 (or_2_out, and_3_out, and_4_out, and_5_out);
  or or_3 (or_3_out, and_6_out, and_7_out);
  or or_4 (or_4_out, and_8_out, and_9_out);
  or or_5 (or_5_out, and_10_out, and_11_out, and_12_out);
  or or_6 (or_6_out, and_13_out, D);
  or or_7 (or_7_out, and_14_out, and_15_out, and_16_out, and_17_out);
  or or_8 (or_8_out, and_18_out, and_19_out, and_20_out);
  _7_Segment_Display #(.active("false")) u_7_segment_display_1 (
    .g(B), .f(nand_1_out), .a(and_1_out), .b(B), .e(or_1_out), .d(and_1_out), .c(and_2_out));  // open: dp
  _7_Segment_Display #(.active("false")) u_7_segment_display_2 (
    .g(or_8_out), .f(or_7_out), .a(or_2_out), .b(or_3_out), .e(or_6_out), .d(or_5_out), .c(or_4_out));  // open: dp
endmodule
